// Logisim project 1.circ as structural Verilog: 1 circuit, main circuit main
module main (
);

  wire button_1_out, button_2_out, transistor_1_out, transistor_2_out, transistor_3_out, transistor_4_out,
       transistor_5_out, transistor_6_out, transistor_8_out, transistor_9_out, transistor_11_out,
       transistor_12_out, transistor_13_out, transistor_14_out, transistor_15_out, transistor_16_out,
       transistor_17_out, transistor_18_out, transistor_20_out, transistor_21_out, transistor_23_out,
       transistor_25_out, transistor_27_out, undriven, undriven_2, undriven_3;

  Transistor #(.gate("br")) transistor_1 (.in(transistor_2_out), .out(transistor_1_out), .gate(button_1_out));
  Transistor #(.gate("br")) transistor_2 (.in(transistor_3_out), .out(transistor_2_out), .gate(button_1_out));
  Transistor #(.\type ("n"), .gate("br")) transistor_3 (
    .in(transistor_4_out), .out(transistor_3_out), .gate(button_1_out));
  Transistor #(.\type ("n"), .gate("br")) transistor_4 (.in(1'b1), .out(transistor_4_out), .gate(button_1_out));
  Button button_1 (.out(button_1_out));
  Transistor #(.\type ("n"), .gate("br")) transistor_5 (
    .in(transistor_6_out), .out(transistor_5_out), .gate(transistor_9_out));
  Transistor #(.gate("br")) transistor_6 (.in(1'b1), .out(transistor_6_out), .gate(button_1_out));
  Transistor #(.gate("br")) transistor_7 (.in(transistor_8_out), .out(transistor_1_out), .gate(transistor_16_out));
  Transistor transistor_8 (.in(transistor_9_out), .out(transistor_8_out), .gate(transistor_15_out));
  Transistor #(.\type ("n"), .gate("br")) transistor_9 (
    .in(transistor_11_out), .out(transistor_9_out), .gate(transistor_16_out));
  Transistor #(.\type ("n")) transistor_10 (.in(transistor_12_out), .out(transistor_9_out), .gate(transistor_15_out));
  Transistor #(.gate("br")) transistor_11 (.in(transistor_14_out), .out(transistor_11_out), .gate(1'b1));
  Transistor #(.\type ("n")) transistor_12 (.in(transistor_13_out), .out(transistor_12_out), .gate(button_2_out));
  Transistor transistor_13 (.in(transistor_15_out), .out(transistor_13_out), .gate(1'b1));
  Transistor #(.\type ("n"), .gate("br")) transistor_14 (
    .in(transistor_16_out), .out(transistor_14_out), .gate(button_2_out));
  Transistor transistor_15 (.in(transistor_17_out), .out(transistor_15_out), .gate(button_2_out));
  Transistor #(.\type ("n"), .gate("br")) transistor_16 (.in(transistor_18_out), .out(transistor_16_out), .gate(1'b1));
  Transistor #(.\type ("n")) transistor_17 (.in(1'b1), .out(transistor_17_out), .gate(1'b1));
  Transistor #(.gate("br")) transistor_18 (.in(1'b1), .out(transistor_18_out), .gate(button_2_out));
  Button button_2 (.out(button_2_out));
  Transistor #(.gate("br")) transistor_19 (.in(transistor_20_out), .out(transistor_1_out), .gate(transistor_9_out));
  Transistor #(.\type ("n"), .gate("br")) transistor_20 (
    .in(transistor_5_out), .out(transistor_20_out), .gate(button_1_out));
  Transistor #(.\type ("n")) transistor_21 (.in(1'b1), .out(transistor_21_out), .gate(transistor_5_out));
  Transistor #(.\type ("n"), .gate("br")) transistor_22 (.in(1'b1), .out(transistor_21_out), .gate(transistor_3_out));
  LED led_1 (.in(transistor_21_out));
  Transistor #(.gate("br")) transistor_23 (.in(transistor_21_out), .out(transistor_23_out), .gate(transistor_3_out));
  Transistor transistor_24 (.in(transistor_23_out), .out(transistor_1_out), .gate(transistor_5_out));
  Transistor #(.\type ("n"), .gate("br")) transistor_25 (.in(undriven_2), .out(transistor_25_out), .gate(undriven_3));
  Transistor #(.\type ("n")) transistor_26 (.in(undriven_2), .out(transistor_25_out), .gate(undriven));
  Transistor #(.gate("br")) transistor_27 (.in(transistor_25_out), .out(transistor_27_out), .gate(undriven_3));
  Transistor transistor_28 (.in(transistor_27_out), .gate(undriven));  // open: out
  // also tied to GND on the sheet: transistor_1_out

  // Notes on the sheet:
  //   A        B                       C        D
endmodule
