// Logisim project CPU.circ as structural Verilog: 5 circuits, main circuit main
module main (
);

  wire and_1_out, and_2_out, Clock_out, cmp_output, decoder_1_out0, decoder_1_out1, program_logic_1_compare,
       program_logic_1_reg1_read_en, program_logic_1_reg2_read_en, program_logic_1_reg_bank_sel,
       program_logic_1_reg_write_en, Reset_out;
  wire [1:0] program_logic_1_reg1_sel, program_logic_1_reg2_sel;
  wire [3:0] multiplexer_1_out, multiplexer_2_out, multiplexer_3_out, program_logic_1_output1,
       register_bank_1_arithmatic_value, register_bank_1_reg1_output, register_bank_1_reg2_output,
       register_bank_2_arithmatic_value, register_bank_2_reg1_output, register_bank_2_reg2_output;

  Program_Logic program_logic_1 (
    .clock(Clock_out), .reset(Reset_out), .Output1(program_logic_1_output1),
    .Reg2_Sel(program_logic_1_reg2_sel), .Reg1_Sel(program_logic_1_reg1_sel),
    .Reg2_Read_En(program_logic_1_reg2_read_en), .Reg1_Read_En(program_logic_1_reg1_read_en),
    .Reg_Write_En(program_logic_1_reg_write_en), .Compare(program_logic_1_compare),
    .Jmp_Fnct_Sel(cmp_output), .Jmp_En(cmp_output), .Reg_Input_1(multiplexer_1_out),
    .Reg_Input_2(multiplexer_2_out), .Reg_Bank_Sel(program_logic_1_reg_bank_sel),
    .Arith_Fn_Sel(program_logic_1_reg1_sel), .Arith_In(multiplexer_3_out));  // open: Output2
  Button Clock (.out(Clock_out));
  Button Reset (.out(Reset_out));
  Decoder #(.enable("false")) decoder_1 (
    .out0(decoder_1_out0), .out1(decoder_1_out1), .sel(program_logic_1_reg_bank_sel));
  Register_Bank register_bank_1 (
    .reset(Reset_out), .Write_Select(program_logic_1_reg1_sel), .Write_Enable(and_1_out),
    .Input(program_logic_1_output1), .Reg1_Output(register_bank_1_reg1_output),
    .Read_Reg1_En(program_logic_1_reg1_read_en), .Read_Reg1_Sel(program_logic_1_reg1_sel),
    .Reg2_Output(register_bank_1_reg2_output), .Read_Reg2_En(program_logic_1_reg2_read_en),
    .Read_Reg2_Sel(program_logic_1_reg2_sel), .Arithmatic_Value(register_bank_1_arithmatic_value),
    .Arith_Fn_Sel(program_logic_1_reg1_sel));  // open: Reg_11, Reg_10, Reg_01, Reg_00
  and and_1 (and_1_out, program_logic_1_reg_write_en, decoder_1_out0);
  Register_Bank register_bank_2 (
    .reset(Reset_out), .Write_Select(program_logic_1_reg1_sel), .Write_Enable(and_2_out),
    .Input(program_logic_1_output1), .Reg1_Output(register_bank_2_reg1_output),
    .Read_Reg1_En(program_logic_1_reg1_read_en), .Read_Reg1_Sel(program_logic_1_reg1_sel),
    .Reg2_Output(register_bank_2_reg2_output), .Read_Reg2_En(program_logic_1_reg2_read_en),
    .Read_Reg2_Sel(program_logic_1_reg2_sel), .Arithmatic_Value(register_bank_2_arithmatic_value),
    .Arith_Fn_Sel(program_logic_1_reg1_sel));  // open: Reg_11, Reg_10, Reg_01, Reg_00
  and and_2 (and_2_out, program_logic_1_reg_write_en, decoder_1_out1);
  cmp cmp (.En(program_logic_1_compare), .Input_1(multiplexer_1_out), .Input_2(multiplexer_2_out), .Output(cmp_output));
  Multiplexer #(.width(4), .enable("false")) multiplexer_1 (
    .in0(register_bank_1_reg1_output), .in1(register_bank_2_reg1_output), .out(multiplexer_1_out),
    .sel(program_logic_1_reg_bank_sel));
  Multiplexer #(.width(4), .enable("false")) multiplexer_2 (
    .in0(register_bank_1_reg2_output), .in1(register_bank_2_reg2_output), .out(multiplexer_2_out),
    .sel(program_logic_1_reg_bank_sel));
  Multiplexer #(.width(4), .enable("false")) multiplexer_3 (
    .in0(register_bank_1_arithmatic_value), .in1(register_bank_2_arithmatic_value), .out(multiplexer_3_out),
    .sel(program_logic_1_reg_bank_sel));
  // Probe on register_bank_1_reg1_output
  // Probe on register_bank_1_reg2_output
  // Probe on register_bank_1_arithmatic_value
  // Probe on register_bank_2_reg1_output
  // Probe on register_bank_2_reg2_output
  // Probe on register_bank_2_arithmatic_value

  // Notes on the sheet:
  //   Program Logic
  //   Register Bank 1
  //   Register Bank 2
endmodule

module Program_Logic (
  input  [3:0] Reg_Input_1,
  input  [3:0] Reg_Input_2,
  input  clock,
  input  reset,
  input  [3:0] Arith_In,
  input  Jmp_En,
  input  Jmp_Fnct_Sel,
  output [3:0] Output1,
  output [3:0] Output2,
  output [1:0] Reg2_Sel,
  output [1:0] Reg1_Sel,
  output [1:0] Arith_Fn_Sel,
  output Reg_Bank_Sel,
  output Reg2_Read_En,
  output Reg1_Read_En,
  output Reg_Write_En,
  output Compare
);

  wire not_1_out, or_1_out;
  wire [0:0] or_2_out;
  wire [3:0] multiplexer_3_out, register_2_q;
  wire [7:0] arithmics_1_output, multiplexer_1_out, register_1_q;
  wire [23:0] rom_1_data;

  Multiplexer #(.width(8), .enable("false")) multiplexer_1 (
    .in0(8'h1), .in1({4'b0000, Output1}), .out(multiplexer_1_out), .sel(or_1_out));
  Arithmics arithmics_1 (
    .Input_1(register_1_q), .Input_2(multiplexer_1_out), .Function_Select({1'b0, or_2_out[0]}),
    .Output(arithmics_1_output));
  // Probe on arithmics_1_output
  or or_1 (or_1_out, rom_1_data[23], Jmp_En);
  or or_2 (or_2_out[0], rom_1_data[22], Jmp_Fnct_Sel);
  Register register_1 (.D(arithmics_1_output), .Q(register_1_q), .clk(clock), .clr(reset));  // open: en
  Register #(.width(4)) register_2 (.D(Arith_In), .en(not_1_out), .Q(register_2_q), .clk(reset), .clr(clock));
  not not_1 (not_1_out, reset);
  Multiplexer #(.width(4), .enable("false")) multiplexer_2 (
    .in0(multiplexer_3_out), .in1(register_2_q), .out(Output1), .sel(rom_1_data[16]));
  Multiplexer #(.width(4), .disabled(0), .enable("false")) multiplexer_3 (
    .in0(rom_1_data[7:4]), .in1(Reg_Input_1), .out(multiplexer_3_out), .sel(rom_1_data[13]));
  ROM #(.dataWidth(24)) rom_1 (
    .addr(register_1_q),
    .data({rom_1_data[23:22], Compare, Reg_Write_En, Reg1_Read_En, Reg2_Read_En, Reg_Bank_Sel, rom_1_data[16], Arith_Fn_Sel, rom_1_data[13:12], Reg1_Sel, Reg2_Sel, rom_1_data[7:0]}));  // open: sel
  Multiplexer #(.width(4), .disabled(0), .enable("false")) multiplexer_4 (
    .in0(rom_1_data[3:0]), .in1(Reg_Input_2), .out(Output2), .sel(rom_1_data[12]));
endmodule

module Register_Bank (
  input  [1:0] Arith_Fn_Sel,
  input  [1:0] Write_Select,
  input  Write_Enable,
  input  Read_Reg1_En,
  input  [1:0] Read_Reg1_Sel,
  input  Read_Reg2_En,
  input  [3:0] Input,
  input  reset,
  input  [1:0] Read_Reg2_Sel,
  output [3:0] Arithmatic_Value,
  output [3:0] Reg1_Output,
  output [3:0] Reg_11,
  output [3:0] Reg_10,
  output [3:0] Reg_01,
  output [3:0] Reg_00,
  output [3:0] Reg2_Output
);

  wire decoder_1_out0, decoder_1_out1, decoder_1_out2, decoder_1_out3, not_1_out, not_2_out, not_3_out,
       not_4_out;
  wire [3:0] arithmics_1_output;

  Decoder #(.select(2), .disabled(0)) decoder_1 (
    .out0(decoder_1_out0), .out1(decoder_1_out1), .out2(decoder_1_out2), .out3(decoder_1_out3),
    .sel(Write_Select), .en(Write_Enable));
  not not_1 (not_1_out, decoder_1_out3);
  Register #(.width(4), .trigger("high")) register_1 (
    .D(Input), .en(not_1_out), .Q(Reg_11), .clk(decoder_1_out3), .clr(reset));
  Register #(.width(4), .trigger("high")) register_2 (
    .D(Input), .en(not_2_out), .Q(Reg_10), .clk(decoder_1_out2), .clr(reset));
  not not_2 (not_2_out, decoder_1_out2);
  not not_3 (not_3_out, decoder_1_out1);
  Arithmics arithmics_1 (
    .Input_1({4'b0000, Reg_01}), .Input_2({4'b0000, Reg_00}), .Function_Select(Arith_Fn_Sel),
    .Output({arithmics_1_output, Arithmatic_Value}));
  Register #(.width(4), .trigger("high")) register_3 (
    .D(Input), .en(not_3_out), .Q(Reg_01), .clk(decoder_1_out1), .clr(reset));
  Register #(.width(4), .trigger("high")) register_4 (
    .D(Input), .en(not_4_out), .Q(Reg_00), .clk(decoder_1_out0), .clr(reset));
  not not_4 (not_4_out, decoder_1_out0);
  Multiplexer #(.select(2), .width(4)) multiplexer_1 (
    .in0(Reg_00), .in1(Reg_01), .in2(Reg_10), .in3(Reg_11), .out(Reg1_Output), .sel(Read_Reg1_Sel),
    .en(Read_Reg1_En));
  Multiplexer #(.select(2), .width(4)) multiplexer_2 (
    .in0(Reg_00), .in1(Reg_01), .in2(Reg_10), .in3(Reg_11), .out(Reg2_Output), .sel(Read_Reg2_Sel),
    .en(Read_Reg2_En));
endmodule

module Arithmics (
  input  [7:0] Input_1,
  input  [7:0] Input_2,
  input  [1:0] Function_Select,
  output [7:0] Output
);

  wire [7:0] adder_1_out, divider_1_out, multiplier_1_out, subtractor_1_out;

  Adder adder_1 (.a(Input_1), .b(Input_2), .out(adder_1_out));  // open: cin, cout
  Subtractor subtractor_1 (.a(Input_1), .b(Input_2), .out(subtractor_1_out));  // open: bin, bout
  Multiplier multiplier_1 (.a(Input_1), .b(Input_2), .out(multiplier_1_out));  // open: cin, cout
  Divider divider_1 (.a(Input_1), .b(Input_2), .out(divider_1_out));  // open: upper, rem
  Multiplexer #(.select(2), .width(8), .enable("false")) multiplexer_1 (
    .in0(adder_1_out), .in1(subtractor_1_out), .in2(multiplier_1_out), .in3(divider_1_out), .out(Output),
    .sel(Function_Select));
endmodule

module cmp (
  input  En,
  input  [3:0] Input_1,
  input  [3:0] Input_2,
  output Output
);

  wire comparator_1_eq, comparator_1_gt, or_1_out;

  Comparator #(.width(4)) comparator_1 (
    .a(Input_1), .b(Input_2), .gt(comparator_1_gt), .eq(comparator_1_eq));  // open: lt
  Multiplexer #(.disabled(0), .enable("false")) multiplexer_1 (.in0(1'b0), .in1(or_1_out), .out(Output), .sel(En));
  or or_1 (or_1_out, comparator_1_gt, comparator_1_eq);
endmodule
